// Logisim project 16-bit ALU.circ as structural Verilog: 7 circuits, main circuit main
module main (
);

  wire button_1_out, clock_1_out;
  wire [2:0] undriven;
  wire [7:0] adder_1_out, register_1_q;
  wire [15:0] n16_bit_b_1_result, ram_1_data, register_file_1_read_data_1, register_file_1_read_data_2;

  Register register_1 (.D(adder_1_out), .Q(register_1_q), .clk(clock_1_out), .clr(button_1_out));  // open: en
  Button button_1 (.out(button_1_out));
  Clock clock_1 (.out(clock_1_out));
  Adder adder_1 (.a(register_1_q), .b(8'h1), .out(adder_1_out));  // open: cin, cout
  RAM #(.dataWidth(16)) ram_1 (.addr(register_1_q), .data(ram_1_data));  // open: sel, clk, ld, clr
  register_file register_file_1 (
    .in_4(n16_bit_b_1_result), .read_data_1(register_file_1_read_data_1),
    .read_data_2(register_file_1_read_data_2), .RA(ram_1_data[3:0]), .write_register(ram_1_data[11:8]),
    .RB(ram_1_data[7:4]));  // open: Clock, regWrite
  // Probe on register_file_1_read_data_1
  // Probe on register_file_1_read_data_2
  _16_bit_b u_16_bit_b_1 (
    .A_2(register_file_1_read_data_1), .B(register_file_1_read_data_2), .Result(n16_bit_b_1_result),
    .Operation(undriven));  // open: Result_2, Cin_3, Cin, Cout, Cout_2
endmodule

// 1- bit
module _1_bit_ALU (
  input  A,
  input  B,
  input  [2:0] Operation,
  input  Cin,
  input  Sub,
  input  Less,
  output Result,
  output Cout,
  output Set
);

  wire AND_out, NOR_out, OR_out, xor_1_out, XOR_2_out;

  xor xor_1 (xor_1_out, B, Sub);
  and AND (AND_out, A, B);
  or OR (OR_out, A, B);
  xor XOR_2 (XOR_2_out, A, B);
  nor NOR (NOR_out, A, B);
  Adder #(.width(1)) adder_1 (.a(A), .b(xor_1_out), .out(Set), .cin(Cin), .cout(Cout));
  Multiplexer #(.select(3)) multiplexer_1 (
    .in0(AND_out), .in1(OR_out), .in2(XOR_2_out), .in3(NOR_out), .in4(Set), .in5(Less), .out(Result),
    .sel(Operation));  // open: in6, in7, en
endmodule

module _16_bits_ALU (
  input  [15:0] A,
  input  [15:0] B,
  input  Sub,
  input  [2:0] Operation,
  output [15:0] result,
  output Zero_flag,
  output Overflow,
  output Cout
);

  wire n1_bit_alu_4_p11, n1_bit_alu_7_p10, n1_bit_alu_7_p12, n1_bit_alu_9_p16, n1_bit_alu_10_p16,
       n1_bit_alu_11_p15, n1_bit_alu_11_p17, n1_bit_alu_13_p19, n1_bit_alu_14_p16, n1_bit_alu_15_p19;

  // _1_bit_ALU 1_bit_alu_1: pin names not known; wires that end beside it: {Operation[2:1], A[7]}, {Operation[2:1], A[7]}, A[0], B[0], A[1], B[1], 1'b0
  // _1_bit_ALU 1_bit_alu_2: pin names not known; wires that end beside it: {Operation[2:1], A[7]}, {Operation[2:1], A[7]}, {Operation[2:1], A[7]}, {Operation[2:1], A[7]}, {Operation[2:1], A[7]}, {Operation[2:1], A[7]}, B[0], A[1], 1'b0, B[2], 1'b0
  // _1_bit_ALU 1_bit_alu_3: pin names not known; wires that end beside it: {Operation[2:1], A[7]}, {Operation[2:1], A[7]}, {Operation[2:1], A[7]}, {Operation[2:1], A[7]}, {Operation[2:1], A[7]}, {Operation[2:1], A[7]}, 1'b0, 1'b0, A[3], B[3], 1'b0
  // _1_bit_ALU 1_bit_alu_4: pin names not known; wires that end beside it: {Operation[2:1], A[7]}, {Operation[2:1], A[7]}, {Operation[2:1], A[7]}, {Operation[2:1], A[7]}, 1'b0, A[3], B[3], 1'b0, B[4], 1'b0, n1_bit_alu_4_p11
  // _1_bit_ALU 1_bit_alu_5: pin names not known; wires that end beside it: {Operation[2:1], A[7]}, {Operation[2:1], A[7]}, {Operation[2:1], A[7]}, {Operation[2:1], A[7]}, A[3], B[3], 1'b0, B[4], 1'b0, A[5], B[5], 1'b0, n1_bit_alu_4_p11, n1_bit_alu_4_p11
  // _1_bit_ALU 1_bit_alu_6: pin names not known; wires that end beside it: {Operation[2:1], A[7]}, {Operation[2:1], A[7]}, {Operation[2:1], A[7]}, {Operation[2:1], A[7]}, {Operation[2:1], A[7]}, {Operation[2:1], A[7]}, B[4], 1'b0, A[5], 1'b0, A[6], B[6], 1'b0, n1_bit_alu_4_p11, n1_bit_alu_4_p11
  // _1_bit_ALU 1_bit_alu_7: pin names not known; wires that end beside it: {Operation[2:1], A[7]}, {Operation[2:1], A[7]}, {Operation[2:1], A[7]}, {Operation[2:1], A[7]}, 1'b0, A[6], 1'b0, B[7], 1'b0, n1_bit_alu_7_p10, n1_bit_alu_7_p10, n1_bit_alu_7_p12
  _1_bit_ALU u_1_bit_alu_8 (.A(A[7]), .B(A[7]), .Sub(A[7]), .Less(A[7]));  // open: Result, Cin, Cout, Operation, Set
  // _1_bit_ALU 1_bit_alu_9: pin names not known; wires that end beside it: {Operation[2:1], A[7]}, {Operation[2:1], A[7]}, {Operation[2:1], A[7]}, {Operation[2:1], A[7]}, {Operation[2:1], A[7]}, result[0], result[1], A[8], B[8], 1'b0, A[9], B[9], 1'b0, {Operation[2:1], A[7]}, n1_bit_alu_7_p12, n1_bit_alu_9_p16, n1_bit_alu_9_p16, {Operation[2:1], A[7]}
  // _1_bit_ALU 1_bit_alu_10: pin names not known; wires that end beside it: {Operation[2:1], A[7]}, {Operation[2:1], A[7]}, result[0], result[1], result[2], {Operation[2:1], A[7]}, B[8], 1'b0, A[9], 1'b0, A[10], B[10], 1'b0, n1_bit_alu_9_p16, n1_bit_alu_9_p16, n1_bit_alu_10_p16, n1_bit_alu_10_p16
  // _1_bit_ALU 1_bit_alu_11: pin names not known; wires that end beside it: {Operation[2:1], A[7]}, {Operation[2:1], A[7]}, result[1], result[2], result[3], {Operation[2:1], A[7]}, A[11], 1'b0, A[10], 1'b0, B[11], 1'b0, n1_bit_alu_10_p16, n1_bit_alu_10_p16, n1_bit_alu_11_p15, n1_bit_alu_11_p15, n1_bit_alu_11_p17
  // _1_bit_ALU 1_bit_alu_12: pin names not known; wires that end beside it: n1_bit_alu_4_p11, {Operation[2:1], A[7]}, {Operation[2:1], A[7]}, result[2], result[3], result[4], {Operation[2:1], A[7]}, A[10], 1'b0, A[11], B[11], 1'b0, A[12], B[12], 1'b0, n1_bit_alu_11_p15, n1_bit_alu_11_p15, n1_bit_alu_11_p17, n1_bit_alu_11_p17
  // _1_bit_ALU 1_bit_alu_13: pin names not known; wires that end beside it: n1_bit_alu_4_p11, n1_bit_alu_4_p11, {Operation[2:1], A[7]}, {Operation[2:1], A[7]}, result[3], result[4], result[5], {Operation[2:1], A[7]}, {Operation[2:1], A[7]}, B[11], 1'b0, A[12], 1'b0, A[13], B[13], 1'b0, n1_bit_alu_11_p17, n1_bit_alu_11_p17, n1_bit_alu_13_p19, n1_bit_alu_13_p19
  // _1_bit_ALU 1_bit_alu_14: pin names not known; wires that end beside it: n1_bit_alu_4_p11, n1_bit_alu_4_p11, n1_bit_alu_7_p10, result[5], result[6], result[4], {Operation[2:1], A[7]}, 1'b0, A[13], 1'b0, A[14], B[14], 1'b0, n1_bit_alu_13_p19, n1_bit_alu_13_p19, n1_bit_alu_14_p16, n1_bit_alu_14_p16
  // _1_bit_ALU 1_bit_alu_15: pin names not known; wires that end beside it: n1_bit_alu_7_p10, n1_bit_alu_7_p10, n1_bit_alu_7_p12, {Operation[2:1], A[7]}, {Operation[2:1], A[7]}, result[5], result[6], result[7], {Operation[2:1], A[7]}, {Operation[2:1], A[7]}, 1'b0, A[14], 1'b0, A[15], B[15], 1'b0, n1_bit_alu_14_p16, n1_bit_alu_14_p16, n1_bit_alu_15_p19, n1_bit_alu_15_p19
  // _1_bit_ALU 1_bit_alu_16: pin names not known; wires that end beside it: n1_bit_alu_7_p10, n1_bit_alu_7_p10, n1_bit_alu_7_p12, {Operation[2:1], A[7]}, {Operation[2:1], A[7]}, result[7], result[6], 1'b0, A[15], 1'b0, {Operation[2:1], A[7]}, {Operation[2:1], A[7]}, n1_bit_alu_15_p19, n1_bit_alu_15_p19, Cout, {Operation[2:1], A[7]}, {Operation[2:1], A[7]}, {Operation[2:1], A[7]}
  xor xor_1 (Overflow, n1_bit_alu_15_p19, Cout);
  nor nor_1 (Zero_flag, result[0], result[1], result[2], result[3], result[4], result[5], result[6], result[7], result[8], result[9], result[10], result[11], result[12], result[13], result[14], result[15]);
  // Pins of 1 and 3 bits meet at {Operation[2:1], A[7]}

  assign {A[4], A[2]} = {2{A[7]}};
  assign Operation[0] = A[7];
  assign Sub = A[7];

  // Other names for the same wires on the sheet: A2[2:0] = {Operation[2:1], A[7]}; A4[2:0] = {Operation[2:1], A[7]};
  //   A7[2:0] = {Operation[2:1], A[7]}
endmodule

// ALU
module _16_bit_b (
  input  [15:0] A,
  input  [15:0] A_2,
  input  [15:0] B,
  input  [2:0] Operation,
  input  Cin,
  input  Cin_2,
  input  Cin_3,
  output [15:0] Result,
  output Result_2,
  output Cout,
  output Cout_2
);

  wire comparator_1_gt, comparator_1_lt, undriven_2;
  wire [15:0] adder_1_out, AND_out, bit_extender_1_out, NOR_out, OR_out, subtractor_1_out, undriven, XOR_out;

  assign AND_out = A & B;  // AND_Gate AND, 16 bits wide
  assign OR_out = A | B;  // OR_Gate OR, 16 bits wide
  assign XOR_out = A ^ B;  // XOR_Gate XOR, 16 bits wide
  assign NOR_out = ~(A | B);  // NOR_Gate NOR, 16 bits wide
  Adder #(.width(16)) adder_1 (.a(A), .b(B), .out(adder_1_out), .cin(Cin), .cout(Cout));
  Subtractor #(.width(16)) subtractor_1 (.a(A), .b(B), .out(subtractor_1_out), .bin(Cin_3), .bout(Cout_2));
  Subtractor #(.width(16)) subtractor_2 (.a(A), .b(B), .out(subtractor_1_out), .bin(Cin_3), .bout(Cout_2));
  Comparator #(.width(16)) comparator_1 (
    .a(A), .b(B), .gt(comparator_1_gt), .eq(comparator_1_gt), .lt(comparator_1_lt));
  assign bit_extender_1_out = {{15{1'b0}}, comparator_1_lt};  // Bit_Extender bit_extender_1
  assign bit_extender_1_out = {{15{1'b0}}, comparator_1_lt};  // Bit_Extender bit_extender_2
  Multiplexer #(.select(3), .width(16)) multiplexer_1 (
    .in0(AND_out), .in1(OR_out), .in2(XOR_out), .in3(NOR_out), .in4(adder_1_out), .in5(subtractor_1_out),
    .in6(bit_extender_1_out), .in7(undriven), .out(Result), .sel(Operation), .en(undriven_2));
  Multiplexer #(.select(3), .width(16)) multiplexer_2 (
    .in0(AND_out), .in1(OR_out), .in2(XOR_out), .in3(NOR_out), .in4(adder_1_out), .in5(subtractor_1_out),
    .in6(bit_extender_1_out), .in7(undriven), .out(Result), .sel(Operation), .en(undriven_2));
  nor nor_2 (Result_2, Result[0], Result[1], Result[2], Result[3], Result[4], Result[5], Result[6], Result[7], Result[8], Result[9], Result[10], Result[11], Result[12], Result[13], Result[14], Result[15]);

  assign A_2 = A;
endmodule

module register_file (
  input  [3:0] write_register,
  input  [3:0] RA,
  input  [3:0] RB,
  input  [15:0] in_4,
  input  regWrite,
  input  Clock,
  output [15:0] read_data_1,
  output [15:0] read_data_2
);

  wire and_1_out, and_2_out, and_3_out, and_4_out, and_5_out, and_6_out, and_7_out, and_8_out, and_9_out,
       and_10_out, and_11_out, and_12_out, and_13_out, and_14_out, and_15_out, and_16_out, decoder_1_out0,
       decoder_1_out1, decoder_1_out2, decoder_1_out3, decoder_1_out4, decoder_1_out5, decoder_1_out6,
       decoder_1_out7, decoder_1_out8, decoder_1_out9, decoder_1_out10, decoder_1_out11, decoder_1_out12,
       decoder_1_out13, decoder_1_out14, decoder_1_out15;
  wire [15:0] register_1_q, register_2_q, register_3_q, register_4_q, register_5_q, register_6_q,
       register_7_q, register_8_q, register_9_q, register_10_q, register_11_q, register_12_q, register_13_q,
       register_14_q, register_15_q, register_16_q;

  Decoder #(.select(4)) decoder_1 (
    .out0(decoder_1_out0), .out1(decoder_1_out1), .out2(decoder_1_out2), .out3(decoder_1_out3),
    .out4(decoder_1_out4), .out5(decoder_1_out5), .out6(decoder_1_out6), .out7(decoder_1_out7),
    .out8(decoder_1_out8), .out9(decoder_1_out9), .out10(decoder_1_out10), .out11(decoder_1_out11),
    .out12(decoder_1_out12), .out13(decoder_1_out13), .out14(decoder_1_out14), .out15(decoder_1_out15),
    .sel(write_register));  // open: en
  and and_1 (and_1_out, decoder_1_out0, regWrite);
  and and_2 (and_2_out, decoder_1_out1, regWrite);
  and and_3 (and_3_out, decoder_1_out2, regWrite);
  and and_4 (and_4_out, decoder_1_out3, regWrite);
  and and_5 (and_5_out, decoder_1_out4, regWrite);
  and and_6 (and_6_out, decoder_1_out5, regWrite);
  and and_7 (and_7_out, decoder_1_out6, regWrite);
  and and_8 (and_8_out, decoder_1_out7, regWrite);
  Register #(.width(16)) register_1 (.D(in_4), .Q(register_1_q), .clk(Clock), .clr(and_1_out));  // open: en
  Register #(.width(16)) register_2 (.D(in_4), .Q(register_2_q), .clk(Clock), .clr(and_2_out));  // open: en
  Register #(.width(16)) register_3 (.D(in_4), .Q(register_3_q), .clk(Clock), .clr(and_3_out));  // open: en
  Register #(.width(16)) register_4 (.D(in_4), .Q(register_4_q), .clk(Clock), .clr(and_4_out));  // open: en
  Register #(.width(16)) register_5 (.D(in_4), .Q(register_5_q), .clk(Clock), .clr(and_5_out));  // open: en
  Register #(.width(16)) register_6 (.D(in_4), .Q(register_6_q), .clk(Clock), .clr(and_6_out));  // open: en
  Register #(.width(16)) register_7 (.D(in_4), .Q(register_7_q), .clk(Clock), .clr(and_7_out));  // open: en
  Register #(.width(16)) register_8 (.D(in_4), .Q(register_8_q), .clk(Clock), .clr(and_8_out));  // open: en
  and and_9 (and_9_out, decoder_1_out8, regWrite);
  and and_10 (and_10_out, decoder_1_out9, regWrite);
  and and_11 (and_11_out, decoder_1_out10, regWrite);
  and and_12 (and_12_out, decoder_1_out11, regWrite);
  and and_13 (and_13_out, decoder_1_out12, regWrite);
  and and_14 (and_14_out, decoder_1_out13, regWrite);
  and and_15 (and_15_out, decoder_1_out14, regWrite);
  and and_16 (and_16_out, decoder_1_out15, regWrite);
  Register #(.width(16)) register_9 (.D(in_4), .Q(register_9_q), .clk(Clock), .clr(and_9_out));  // open: en
  Register #(.width(16)) register_10 (.D(in_4), .Q(register_10_q), .clk(Clock), .clr(and_10_out));  // open: en
  Register #(.width(16)) register_11 (.D(in_4), .Q(register_11_q), .clk(Clock), .clr(and_11_out));  // open: en
  Register #(.width(16)) register_12 (.D(in_4), .Q(register_12_q), .clk(Clock), .clr(and_12_out));  // open: en
  Register #(.width(16)) register_13 (.D(in_4), .Q(register_13_q), .clk(Clock), .clr(and_13_out));  // open: en
  Register #(.width(16)) register_14 (.D(in_4), .Q(register_14_q), .clk(Clock), .clr(and_14_out));  // open: en
  Register #(.width(16)) register_15 (.D(in_4), .Q(register_15_q), .clk(Clock), .clr(and_15_out));  // open: en
  Register #(.width(16)) register_16 (.D(in_4), .Q(register_16_q), .clk(Clock), .clr(and_16_out));  // open: en
  Multiplexer #(.select(4), .width(16)) multiplexer_1 (
    .in0(register_1_q), .in1(register_2_q), .in2(register_3_q), .in3(register_4_q), .in4(register_5_q),
    .in5(register_6_q), .in6(register_7_q), .in7(register_8_q), .in8(register_9_q), .in9(register_10_q),
    .in10(register_11_q), .in11(register_12_q), .in12(register_13_q), .in13(register_14_q),
    .in14(register_15_q), .in15(register_16_q), .out(read_data_1), .sel(RA));  // open: en
  Multiplexer #(.select(4), .width(16)) multiplexer_2 (
    .in0(register_1_q), .in1(register_2_q), .in2(register_3_q), .in3(register_4_q), .in4(register_5_q),
    .in5(register_6_q), .in6(register_7_q), .in7(register_8_q), .in8(register_9_q), .in9(register_10_q),
    .in10(register_11_q), .in11(register_12_q), .in12(register_13_q), .in13(register_14_q),
    .in14(register_15_q), .in15(register_16_q), .out(read_data_2), .sel(RB));  // open: en
endmodule

module Extend_block (
  input  [7:0] Input_A,
  input  Less,
  output [15:0] Imm16
);

  wire [15:0] bit_extender_1_out, bit_extender_2_out;

  assign bit_extender_1_out = {{8{1'b0}}, Input_A};  // Bit_Extender bit_extender_1
  assign bit_extender_2_out = {{8{Input_A[7]}}, Input_A};  // Bit_Extender bit_extender_2
  Multiplexer #(.width(16), .enable("false")) multiplexer_1 (
    .in0(bit_extender_1_out), .in1(bit_extender_2_out), .out(Imm16), .sel(Less));
endmodule

module Instruction_Block (
  input  [15:0] Instruction,
  output [2:0] Opcode,
  output [2:0] Rs,
  output [2:0] Rt,
  output [2:0] Rd,
  output [1:0] Shift_Amount,
  output [1:0] Function,
  output [6:0] Immediate
);


  assign Function = Instruction[1:0];
  assign Immediate = Instruction[6:0];
  assign Opcode = Instruction[15:13];
  assign Rd = Instruction[6:4];
  assign Rs = Instruction[12:10];
  assign Rt = Instruction[9:7];
  assign Shift_Amount = Instruction[3:2];
endmodule
